# Fritzing sketch Arduino Uno R3 - TEE I2C Keypad (saved by Fritzing 0.9.2b)

parts:
  Keypad1 = I2C KEYPAD
  Part1 = Arduino Uno (Rev3)

nets:
  VIN: Keypad1.VIN, Part1.5V
  N1: Keypad1.SDA, Part1.A4/SDA
  N2: Keypad1.SCL, Part1.A5/SCL
  GND: Keypad1.GND, Part1.GND

custom parts:
  I2C KEYPAD: I2C Keypad
